# Fritzing sketch piSchoolBell (saved by Fritzing 0.9.2b)
breadboards: 1

parts:
  Raspberry_Pi_3_B+ = Raspberry Pi 3 [part_number=RPI-3-V1.2]
  U1_-_LCD_display = LCD-16X2 [package=lcd-16x2_nosilk]
  R1 = Trimmer Potentiometer [maximum_resistance=10kΩ package=THT]
  S1_-_button1 = Pushbutton [package="[THT]"]
  S2_-_button2 = Pushbutton [package="[THT]"]
  Ring_bell = KY-019 5V Relay Module [package="Breakout board"]
  S5_-_ring_off = Toggle Switch [package=THT]
  R2 = Resistor [tolerance=±5% resistance=10k package=THT]
  R3 = Resistor [tolerance=±5% resistance=10k package=THT]
  R4 = Resistor [tolerance=±5% resistance=1k package=THT]
  R5 = Resistor [tolerance=±5% resistance=1k package=THT]
  U2_-_bell_transformer = Transformer [package=transformer_smd]
  ZS-042_RTC1 = ZS-042 RTC Module
  S3_-_button3 = Pushbutton [package="[THT]"]
  R6 = Resistor [tolerance=±5% resistance=10k package=THT]
  R7 = Resistor [tolerance=±5% resistance=1k package=THT]
  S4_-_button4 = Pushbutton [package="[THT]"]
  R8 = Resistor [tolerance=±5% resistance=10k package=THT]
  R9 = Resistor [tolerance=±5% resistance=1k package=THT]

nets:
  3V3: Raspberry_Pi_3_B+.3v3, Raspberry_Pi_3_B+.3V3, U1_-_LCD_display.A, ZS-042_RTC1.VCC
  N1: Raspberry_Pi_3_B+.GPIO2, ZS-042_RTC1.SDA
  N2: Raspberry_Pi_3_B+.GPIO3, ZS-042_RTC1.SCL
  GND: Raspberry_Pi_3_B+.GND, U1_-_LCD_display.VSS, U1_-_LCD_display.R_W, U1_-_LCD_display.K, R1.leg1, S1_-_button1.Pin_1, S1_-_button1.Pin_2, S2_-_button2.Pin_1, S2_-_button2.Pin_2, Ring_bell.-, ZS-042_RTC1.GND, S3_-_button3.Pin_3, S3_-_button3.Pin_4, S4_-_button4.Pin_3, S4_-_button4.Pin_4
  N3: Raspberry_Pi_3_B+.GIPO10, R9.Pin_0
  N4: Raspberry_Pi_3_B+.GIPO9, R7.Pin_0
  N5: Raspberry_Pi_3_B+.GIPO6, U1_-_LCD_display.DB4
  N6: Raspberry_Pi_3_B+.GIPO13, U1_-_LCD_display.DB5
  N7: Raspberry_Pi_3_B+.GIPO19, U1_-_LCD_display.DB6
  N8: Raspberry_Pi_3_B+.GIPO26, U1_-_LCD_display.DB7
  N9: Raspberry_Pi_3_B+.GIPO21, U1_-_LCD_display.E
  N10: Raspberry_Pi_3_B+.GIPO20, U1_-_LCD_display.RS
  N11: Raspberry_Pi_3_B+.GIPO7, R4.Pin_1
  N12: Raspberry_Pi_3_B+.GIPO8, R5.Pin_1
  N13: Raspberry_Pi_3_B+.GIPO15, Ring_bell.S
  5V: Raspberry_Pi_3_B+.5V, U1_-_LCD_display.VDD, R1.leg2, Ring_bell.+, R2.Pin_0, R3.Pin_0, R6.Pin_1, R8.Pin_1
  N14: U1_-_LCD_display.VO, R1.wiper
  N15: S1_-_button1.Pin_3, S1_-_button1.Pin_4, R2.Pin_1, R4.Pin_0
  N16: S2_-_button2.Pin_3, S2_-_button2.Pin_4, R3.Pin_1, R5.Pin_0
  N17: Ring_bell.Common, U2_-_bell_transformer.4
  N18: Ring_bell.NO, S5_-_ring_off.COM
  N19: S3_-_button3.Pin_1, S3_-_button3.Pin_2, R6.Pin_0, R7.Pin_1
  N20: S4_-_button4.Pin_1, S4_-_button4.Pin_2, R8.Pin_0, R9.Pin_1

notes:
  School bell
  Optional RTC module

custom parts:
  KY-019 5V Relay Module: KY-019 5V Relay module, used to control AC circuits.
